# Fritzing sketch distance_sensor (saved by Fritzing 0.9.3b)

parts:
  hc-sr1 = hc-sr04
  Raspberry_Pi_1 = Raspberry Pi 3 [part_number=RPI-3-V1.2]

nets:
  VCC: hc-sr1.VCC, Raspberry_Pi_1.5V
  N1: hc-sr1.Trig, Raspberry_Pi_1.GIPO4, Raspberry_Pi_1.GIPO14
  N2: hc-sr1.Echo, Raspberry_Pi_1.GIPO18
  GND: hc-sr1.GND, Raspberry_Pi_1.GND
